# Fritzing sketch SimpleStateMachine (saved by Fritzing 0.9.4)
breadboards: 1

parts:
  Light = Tantalum Capacitor [capacitance=1μF package="100 mil [THT, tantalum]"]
  Resistor_1 = Resistor [tolerance=±5% resistance=330 package=THT]
  Button = Pushbutton [package="[THT]"]
  Chip = Adafruit HUZZAH32 ESP32 Feather [part_number="Adafruit #3405"]
  R1 = Resistor [tolerance=±5% resistance=220 package=THT]

nets:
  N1: Light.-, R1.Pin_1
  N2: Light.+, Chip.IO12_A11
  N3: Resistor_1.Pin_0, Button.Pin_1, Button.Pin_2, Chip.A0_DAC2
  N4: Button.Pin_3, Button.Pin_4, Chip.3.3V
  N5: Chip.GND, R1.Pin_0

// code stored in the sketch: LEDComplexitySimulation.ino
/*
LEDComplexity.ino
Demonstrate a series of functionality with buttons and switches
*/
  const int InternalLED=13;
  const int ExternalLED=12;

  // A0 has the pushbutton attached to it. Give it a name:
  int pushButton=A0;

  // the setup routine runs once when you press reset:
  void setup() {
   // initialize serial communication at 9600 bits per second:
  Serial.begin(9600);
   // make the pushbutton's pin an input:
  pinMode(pushButton, INPUT);
  pinMode(ExternalLED, OUTPUT);
  pinMode(InternalLED, OUTPUT);
  }

  // the loop routine runs over and over again forever:
  void loop() {
   // read the input pin:
  int buttonState=digitalRead(pushButton);
   // print out the state of the button:
   Serial.println(buttonState);
   delay(1);        // delay in between reads for stability

   if(buttonState==1)
   {
    digitalWrite(ExternalLED, HIGH);    
    digitalWrite(ExternalLED, LOW);
   }
   else
   {
    digitalWrite(ExternalLED, LOW);
   }
  }
